# Fritzing sketch schematic (saved by Fritzing 0.9.2b)
breadboards: 1

parts:
  Part1 = Arduino Uno (Rev3)
  LED1 = smd LED [color="Green (565nm)" package="1206 [SMD]"]
  R1 = Resistor [tolerance=±5% resistance=100 package=THT]
  LED2 = smd LED [color="Yellow (585nm)" package="0603 [SMD]"]
  R2 = Resistor [tolerance=±5% resistance=200 package=THT]
  LED3 = smd LED [color="Red (635nm)" package="0603 [SMD]"]
  R3 = Resistor [tolerance=±5% resistance=200 package=THT]

nets:
  N1: Part1.GND, R1.Pin_0, R2.Pin_0, R3.Pin_0
  N2: Part1.D2, LED1.anode
  N3: Part1.D4, LED2.anode
  N4: Part1.D7, LED3.anode
  N5: LED1.cathode, R1.Pin_1
  N6: LED2.cathode, R2.Pin_1
  N7: LED3.cathode, R3.Pin_1
